# Fritzing sketch Sauna_Steuerung (saved by Fritzing 0.9.4)

parts:
  WeMos_D1_Mini1 = WeMos D1 Mini
  DS1 = DS18B20 1-Wire Temperature Sensor [part_number=DS18B20]
  R1 = Resistor [tolerance=±5% resistance=2.7k package="0402 [SMD]"]
  Bauteil1 = BME280 Breakout
  Q1 = TRANSISTOR_NPN [package=to-92]
  U1 = RELAY-SOLIDSTATE [package=relay-s108t02]
  R2 = Resistor [tolerance=±5% resistance=2.7k package="0402 [SMD]"]
  Bauteil2 = ws2812b [package="smd 2812b"]
  S1 = SWITCH-MOMENTARY-2 [package=reed_switch_plastic]
  RHT1 = Humidity and Temperature Sensor RHT03
  DS2 = DS18B20 1-Wire Temperature Sensor [part_number=DS18B20]

nets:
  VDD: WeMos_D1_Mini1.3V3, DS1.VDD, R1.Pin_0, Bauteil1.3.3V, RHT1.Vcc, DS2.VDD
  5V: WeMos_D1_Mini1.5V, U1.+, Bauteil2.VDD
  N1: WeMos_D1_Mini1.D0, R2.Pin_0
  N2: WeMos_D1_Mini1.D1, Bauteil1.SCK/SCL
  N3: WeMos_D1_Mini1.D2, Bauteil1.SDI/SDA
  N4: WeMos_D1_Mini1.D3, DS1.DQ, R1.Pin_1, DS2.DQ
  N5: WeMos_D1_Mini1.D4, Bauteil2.DIN
  N6: WeMos_D1_Mini1.D5, RHT1.Data-signal
  N7: WeMos_D1_Mini1.D6, S1.1
  GND: WeMos_D1_Mini1.G, DS1.GND, Bauteil1.GND, Q1.E, Bauteil2.VSS, S1.2, RHT1.GND_2, DS2.GND
  N8: Q1.B, R2.Pin_1
  N9: Q1.C, U1.-
